# Fritzing sketch Board (saved by Fritzing 0.9.3b)

parts:
  R1 = Resistor [tolerance=±5% resistance=150 package="0805 [SMD]"]
  R3 = Resistor [tolerance=±5% resistance=150 package="0805 [SMD]"]
  Part4 = Adafruit Trinket 3V [part_number="Adafruit #1500"]
  Part5 = TP4056 Charger
  J1 = Piezo Speaker
  LED1 = RGB LED (com. cathode, rgb) [package="5 mm [THT]"]
  S1 = Toggle Switch [package=THT]
  S2 = Round Pushbutton
  BAT1 = LIPO-1000mAh [package=lipo-1000]

nets:
  N1: R1.Pin_0, LED1.green_anode
  N2: R1.Pin_1, Part4.#4
  N3: R3.Pin_0, LED1.red_anode
  N4: R3.Pin_1, Part4.#3
  N5: Part4.GND, J1.pin1, LED1.common_cathode
  N6: Part4.#0, S2.leg0
  N7: Part4.#1, S2.leg1
  N8: Part4.#2, J1.pin2
  N9: Part4.+3V3, S1.L2
  N10: Part5.BAT+, S1.COM, BAT1.+
  N11: Part5.BAT-, BAT1.-

custom parts:
  Adafruit Trinket 3V: Trinket may be small, but do not be fooled by its size! It's a tiny microcontroller board, built around the Atmel ATtiny85, a little chip with a lot of power. We wanted to design a microcontroller board that was small enough to fit into any project, and low cost enough to use without hesitation. Perfect for when you don't want to give up your expensive dev-board and you aren't willing to take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
